# Fritzing sketch RTKBaseStation (saved by Fritzing 0.9.9b)
breadboards: 1

parts:
  Part1 = Adafruit HUZZAH32 ESP32 Feather [part_number="Adafruit #3405"]
  Qwiic1_to_RTK_board = Qwiic Connector  # not connected
  10_k = Resistor [tolerance=±5% power=0.25 resistance=220 package=THT]
  Wipe = Pushbutton [package="[SMD]"]
  Qwiic2_from_RTK_board = Qwiic Connector  # not connected
  Reset = Pushbutton [package="[SMD]"]
  OLED1 = OLED 128x64 I2C Monochrome Display GND-VDD  # not connected

nets:
  N1: Part1.GND, 10_k.Pin_1, Reset.Pin_1, Reset.Pin_2
  N2: Part1.3.3V, Wipe.Pin_1, Wipe.Pin_2
  N3: Part1.RESET, Reset.Pin_3, Reset.Pin_4
  N4: Part1.IO15_A8, 10_k.Pin_0, Wipe.Pin_3, Wipe.Pin_4

custom parts:
  Qwiic Connector: Qwiic PCB connector
  OLED 128x64 I2C Monochrome Display GND-VDD: OLED 128x64 I2C Monochrome Display. Note: there are two variants of this part, this one is the GND VDD SCK SDA variant. The other is VDD GND SCK SDA. Make sure you select the part that matches your module as using the incorrect part will probably destroy your module! In addition the mounting holes are marked on silkscreen but not by default drilled. If you want drilled mounting holes, copy a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
